# Fritzing sketch schematic (saved by Fritzing 0.9.3b)
breadboards: 1

parts:
  U1 = lolin
  S1 = Round Pushbutton
  S2 = Round Pushbutton
  S3 = Round Pushbutton
  S4 = Round Pushbutton
  S5 = Round Pushbutton
  S6 = Round Pushbutton
  U2 = LIPO-110mAh [package=lipo-110]
  U3 = SWITCH_SPDT [package=kps-1290]

nets:
  N1: U1.connector11, S3.leg1
  N2: U1.connector12, S2.leg1
  N3: U1.connector13, S1.leg1
  N4: U1.connector15, S1.leg0, S2.leg0, S3.leg0
  N5: U1.connector16, U2.-
  N6: U1.connector17, U3.S
  N7: U1.connector20, S4.leg1, S5.leg1, S6.leg1
  N8: U1.connector22, S4.leg0
  N9: U1.connector23, S5.leg0
  N10: U1.connector24, S6.leg0
  N11: U2.+, U3.P
